// Logisim project cpu.circ as structural Verilog: 5 circuits, main circuit main
module main (
  input  [31:0] INSTRUCTION,
  input  CLOCK,
  output [31:0] PROGRAM_COUNTER,
  output [31:0] ra,
  output [31:0] sp,
  output [31:0] t0,
  output [31:0] t1,
  output [31:0] t2,
  output [31:0] s0,
  output [31:0] s1,
  output [31:0] a0
);

  wire ASel, BrEq, BrLt, BrUn, BSel, MemRW, PCSel, RegWEn, UType;
  wire [1:0] DataSize, WBSel;
  wire [2:0] funct3, ImmSel;
  wire [3:0] ALUSel;
  wire [4:0] rd, rs1, rs2;
  wire [6:0] funct7, opcode;
  wire [31:0] adder_1_out, Arithmetic_Logic_Unit_result, DMEM_p5, immgen_1_immediate, memory_1_dataout,
       multiplexer_1_out, multiplexer_2_out, multiplexer_3_out, multiplexer_4_out, multiplexer_5_out,
       multiplexer_6_out, RegFile_read_data_1, RegFile_read_data_2, register_1_q;

  Adder #(.width(32)) adder_1 (.a(PROGRAM_COUNTER), .b(32'h4), .out(adder_1_out));  // open: cin, cout
  Multiplexer #(.width(32), .enable("false")) multiplexer_1 (
    .in0(Arithmetic_Logic_Unit_result), .in1(adder_1_out), .out(multiplexer_1_out), .sel(PCSel));
  Register #(.width(32)) PC (.D(multiplexer_1_out), .clk(CLOCK), .Q(PROGRAM_COUNTER));  // open: en, clr
  control control_1 (
    .OPCODE(opcode), .FUNCT3(funct3), .FUNCT7(funct7), .BrEq(BrEq), .BrLt(BrLt), .ALUSel(ALUSel),
    .ImmSel(ImmSel), .RegWEn(RegWEn), .ASel(ASel), .BSel(BSel), .BrUn(BrUn), .WBSel(WBSel), .MemRW(MemRW),
    .PCSel(PCSel), .UType(UType), .DataSize(DataSize));
  Multiplexer #(.width(32), .enable("false")) multiplexer_2 (
    .in0(32'h13), .in1(INSTRUCTION), .out(multiplexer_2_out), .sel(PCSel));
  Register #(.width(32)) register_1 (.D(PROGRAM_COUNTER), .clk(CLOCK), .Q(register_1_q));  // open: en, clr
  Register #(.width(32)) register_2 (
    .D(multiplexer_2_out), .clk(CLOCK), .Q({funct7, rs2, rs1, funct3, rd, opcode}));  // open: en, clr
  immgen immgen_1 (
    .INSTRUCTION({funct7, rs2, rs1, funct3, rd, opcode}), .IMMSEL(ImmSel), .Immediate(immgen_1_immediate));
  Multiplexer #(.width(32), .enable("false")) multiplexer_3 (
    .in0(multiplexer_6_out), .in1(immgen_1_immediate), .out(multiplexer_3_out), .sel(UType));
  regfile_main RegFile (
    .rs2(rs2), .rd(rd), .Read_Data_1(RegFile_read_data_1), .Read_Data_2(RegFile_read_data_2), .ra(ra),
    .sp(sp), .t0(t0), .t1(t1), .t2(t2), .s0(s0), .s1(s1), .a0(a0), .rs1(rs1), .Write_Data(multiplexer_3_out),
    .RegWEn(RegWEn), .clk(CLOCK));
  Multiplexer #(.width(32), .enable("false")) multiplexer_4 (
    .in0(register_1_q), .in1(RegFile_read_data_1), .out(multiplexer_4_out), .sel(ASel));
  branch branch_1 (.rs1(RegFile_read_data_1), .rs2(RegFile_read_data_2), .in_3(BrUn), .BrEq(BrEq), .BrLt(BrLt));
  Multiplexer #(.width(32), .enable("false")) multiplexer_5 (
    .in0(RegFile_read_data_2), .in1(immgen_1_immediate), .out(multiplexer_5_out), .sel(BSel));
  alu Arithmetic_Logic_Unit (
    .B(multiplexer_5_out), .Result(Arithmetic_Logic_Unit_result), .A(multiplexer_4_out), .ALUSel(ALUSel));
  // mem_main DMEM: pin names not known; wires that end beside it: Arithmetic_Logic_Unit_result, RegFile_read_data_2, CLOCK, MemRW, DMEM_p5
  memory memory_1 (
    .Address(Arithmetic_Logic_Unit_result), .DataIn(DMEM_p5), .DataSize(DataSize), .DataOut(memory_1_dataout));
  Multiplexer #(.select(2), .width(32), .enable("false")) multiplexer_6 (
    .in0(Arithmetic_Logic_Unit_result), .in1(memory_1_dataout), .in2(PROGRAM_COUNTER),
    .out(multiplexer_6_out), .sel(WBSel));  // open: in3

  // Other names for the same wires on the sheet: clk = CLOCK

  // Notes on the sheet:
  //   Output
  //   IMEM (do **NOT** move this)
  //   Inputs
  //   Inputs/Outputs for testing. Do **NOT** move these.
endmodule

module control (
  input  [6:0] OPCODE,
  input  [2:0] FUNCT3,
  input  [6:0] FUNCT7,
  input  BrEq,
  input  BrLt,
  output [3:0] ALUSel,
  output [2:0] ImmSel,
  output RegWEn,
  output ASel,
  output BSel,
  output BrUn,
  output [1:0] WBSel,
  output MemRW,
  output PCSel,
  output UType,
  output [1:0] DataSize
);

  wire and_1_out, and_2_out, and_3_out, and_4_out, and_5_out, and_6_out, and_7_out, and_8_out, and_9_out,
       and_10_out, and_11_out, and_12_out, and_13_out, and_14_out, and_15_out, and_16_out, and_17_out,
       and_18_out, and_19_out, and_20_out, and_21_out, and_22_out, and_23_out, and_24_out, and_25_out,
       and_26_out, and_27_out, and_28_out, and_29_out, and_30_out, and_31_out, and_32_out, and_33_out,
       and_34_out, and_35_out, and_36_out, and_37_out, and_38_out, and_39_out, and_40_out, and_41_out,
       and_42_out, and_43_out, and_44_out, and_45_out, and_46_out, and_47_out, and_48_out, and_49_out,
       and_50_out, and_51_out, and_52_out, and_53_out, and_54_out, and_55_out, and_56_out, and_57_out,
       and_58_out, and_59_out, BType, comparator_1_eq, comparator_2_eq, comparator_3_eq, comparator_4_eq,
       comparator_5_eq, comparator_6_eq, comparator_7_eq, comparator_8_eq, comparator_9_eq, comparator_10_eq,
       comparator_11_eq, comparator_12_eq, comparator_13_eq, comparator_14_eq, comparator_15_eq,
       comparator_16_eq, comparator_17_eq, comparator_18_eq, comparator_19_eq, comparator_20_eq,
       comparator_21_eq, comparator_22_eq, comparator_23_eq, comparator_24_eq, comparator_25_eq,
       comparator_26_eq, comparator_27_eq, comparator_28_eq, comparator_29_eq, comparator_31_eq,
       comparator_32_eq, comparator_33_eq, comparator_34_eq, comparator_35_eq, comparator_36_eq,
       comparator_37_eq, comparator_38_eq, comparator_39_eq, comparator_40_eq, comparator_41_eq,
       comparator_42_eq, comparator_43_eq, comparator_44_eq, comparator_45_eq, comparator_46_eq,
       comparator_47_eq, comparator_48_eq, comparator_49_eq, comparator_50_eq, comparator_51_eq,
       comparator_52_eq, comparator_53_eq, comparator_54_eq, comparator_55_eq, comparator_57_eq,
       comparator_58_eq, comparator_59_eq, comparator_60_eq, comparator_61_eq, comparator_62_eq,
       comparator_63_eq, comparator_64_eq, comparator_65_eq, comparator_66_eq, comparator_68_eq,
       comparator_69_eq, comparator_70_eq, comparator_71_eq, comparator_72_eq, comparator_73_eq,
       comparator_74_eq, comparator_75_eq, IType, jal, jalr, lb, lh, lui, lw, not_1_out, not_2_out,
       not_3_out, not_4_out, RType, sw;

  Comparator #(.width(3), .mode("unsigned")) comparator_1 (
    .a(FUNCT3), .b(3'b000), .eq(comparator_1_eq));  // open: gt, lt
  Comparator #(.width(7), .mode("unsigned")) comparator_2 (
    .a(FUNCT7), .b({7{1'b0}}), .eq(comparator_2_eq));  // open: gt, lt
  Comparator #(.width(3), .mode("unsigned")) comparator_3 (
    .a(FUNCT3), .b(3'b000), .eq(comparator_3_eq));  // open: gt, lt
  Comparator #(.width(7), .mode("unsigned")) comparator_4 (
    .a(FUNCT7), .b(7'b0000001), .eq(comparator_4_eq));  // open: gt, lt
  Comparator #(.width(3), .mode("unsigned")) comparator_5 (
    .a(FUNCT3), .b(3'b000), .eq(comparator_5_eq));  // open: gt, lt
  Comparator #(.width(7), .mode("unsigned")) comparator_6 (
    .a(FUNCT7), .b(7'b0100000), .eq(comparator_6_eq));  // open: gt, lt
  Comparator #(.width(3), .mode("unsigned")) comparator_7 (
    .a(FUNCT3), .b(3'b001), .eq(comparator_7_eq));  // open: gt, lt
  Comparator #(.width(7), .mode("unsigned")) comparator_8 (
    .a(FUNCT7), .b({7{1'b0}}), .eq(comparator_8_eq));  // open: gt, lt
  Comparator #(.width(3), .mode("unsigned")) comparator_9 (
    .a(FUNCT3), .b(3'b001), .eq(comparator_9_eq));  // open: gt, lt
  Comparator #(.width(7), .mode("unsigned")) comparator_10 (
    .a(FUNCT7), .b(7'b0000001), .eq(comparator_10_eq));  // open: gt, lt
  Comparator #(.width(3), .mode("unsigned")) comparator_11 (
    .a(FUNCT3), .b(3'b011), .eq(comparator_11_eq));  // open: gt, lt
  Comparator #(.width(7), .mode("unsigned")) comparator_12 (
    .a(FUNCT7), .b(7'b0000001), .eq(comparator_12_eq));  // open: gt, lt
  Comparator #(.width(3), .mode("unsigned")) comparator_13 (
    .a(FUNCT3), .b(3'b010), .eq(comparator_13_eq));  // open: gt, lt
  Comparator #(.width(7), .mode("unsigned")) comparator_14 (
    .a(FUNCT7), .b({7{1'b0}}), .eq(comparator_14_eq));  // open: gt, lt
  Comparator #(.width(3), .mode("unsigned")) comparator_15 (
    .a(FUNCT3), .b(3'b100), .eq(comparator_15_eq));  // open: gt, lt
  Comparator #(.width(7), .mode("unsigned")) comparator_16 (
    .a(FUNCT7), .b({7{1'b0}}), .eq(comparator_16_eq));  // open: gt, lt
  Comparator #(.width(3), .mode("unsigned")) comparator_17 (
    .a(FUNCT3), .b(3'b101), .eq(comparator_17_eq));  // open: gt, lt
  Comparator #(.width(7), .mode("unsigned")) comparator_18 (
    .a(FUNCT7), .b(7'b0000001), .eq(comparator_18_eq));  // open: gt, lt
  Comparator #(.width(3), .mode("unsigned")) comparator_19 (
    .a(FUNCT3), .b(3'b101), .eq(comparator_19_eq));  // open: gt, lt
  Comparator #(.width(7), .mode("unsigned")) comparator_20 (
    .a(FUNCT7), .b({7{1'b0}}), .eq(comparator_20_eq));  // open: gt, lt
  Comparator #(.width(3), .mode("unsigned")) comparator_21 (
    .a(FUNCT3), .b(3'b110), .eq(comparator_21_eq));  // open: gt, lt
  Comparator #(.width(7), .mode("unsigned")) comparator_22 (
    .a(FUNCT7), .b({7{1'b0}}), .eq(comparator_22_eq));  // open: gt, lt
  Comparator #(.width(3), .mode("unsigned")) comparator_23 (
    .a(FUNCT3), .b(3'b111), .eq(comparator_23_eq));  // open: gt, lt
  Comparator #(.width(7), .mode("unsigned")) comparator_24 (
    .a(FUNCT7), .b(7'b0000001), .eq(comparator_24_eq));  // open: gt, lt
  Comparator #(.width(3), .mode("unsigned")) comparator_25 (
    .a(FUNCT3), .b(3'b111), .eq(comparator_25_eq));  // open: gt, lt
  Comparator #(.width(7), .mode("unsigned")) comparator_26 (
    .a(FUNCT7), .b({7{1'b0}}), .eq(comparator_26_eq));  // open: gt, lt
  and and_1 (and_1_out, comparator_1_eq, comparator_2_eq);
  and and_2 (and_2_out, comparator_3_eq, comparator_4_eq);
  and and_3 (and_3_out, comparator_5_eq, comparator_6_eq);
  and and_4 (and_4_out, comparator_7_eq, comparator_8_eq);
  and and_5 (and_5_out, comparator_9_eq, comparator_10_eq);
  and and_6 (and_6_out, comparator_11_eq, comparator_12_eq);
  and and_7 (and_7_out, comparator_13_eq, comparator_14_eq);
  and and_8 (and_8_out, comparator_15_eq, comparator_16_eq);
  and and_9 (and_9_out, comparator_17_eq, comparator_18_eq);
  and and_10 (and_10_out, comparator_19_eq, comparator_20_eq);
  and and_11 (and_11_out, comparator_21_eq, comparator_22_eq);
  and and_12 (and_12_out, comparator_23_eq, comparator_24_eq);
  and and_13 (and_13_out, comparator_25_eq, comparator_26_eq);
  Multiplexer #(.width(4), .enable("false")) multiplexer_1 (
    .in1(4'b0000), .out(ALUSel), .sel(and_14_out));  // open: in0
  and and_14 (and_14_out, and_1_out, RType);
  Multiplexer #(.width(4), .enable("false")) multiplexer_2 (
    .in1(4'b1010), .out(ALUSel), .sel(and_15_out));  // open: in0
  and and_15 (and_15_out, and_2_out, RType);
  Multiplexer #(.width(4), .enable("false")) multiplexer_3 (
    .in1(4'b1100), .out(ALUSel), .sel(and_16_out));  // open: in0
  and and_16 (and_16_out, and_3_out, RType);
  Multiplexer #(.width(4), .enable("false")) multiplexer_4 (
    .in1(4'b0110), .out(ALUSel), .sel(and_17_out));  // open: in0
  and and_17 (and_17_out, and_4_out, RType);
  Multiplexer #(.width(4), .enable("false")) multiplexer_5 (
    .in1(4'b1110), .out(ALUSel), .sel(and_18_out));  // open: in0
  and and_18 (and_18_out, and_5_out, RType);
  Multiplexer #(.width(4), .enable("false")) multiplexer_6 (
    .in1(4'b1011), .out(ALUSel), .sel(and_19_out));  // open: in0
  and and_19 (and_19_out, and_6_out, RType);
  Multiplexer #(.width(4), .enable("false")) multiplexer_7 (
    .in1(4'b0111), .out(ALUSel), .sel(and_20_out));  // open: in0
  and and_20 (and_20_out, and_7_out, RType);
  Multiplexer #(.width(4), .enable("false")) multiplexer_8 (
    .in1(4'b0011), .out(ALUSel), .sel(and_21_out));  // open: in0
  and and_21 (and_21_out, and_8_out, RType);
  Multiplexer #(.width(4), .enable("false")) multiplexer_9 (
    .in1(4'b1000), .out(ALUSel), .sel(and_22_out));  // open: in0
  and and_22 (and_22_out, and_9_out, RType);
  Multiplexer #(.width(4), .enable("false")) multiplexer_10 (
    .in1(4'b0100), .out(ALUSel), .sel(and_23_out));  // open: in0
  and and_23 (and_23_out, and_10_out, RType);
  Multiplexer #(.width(4), .enable("false")) multiplexer_11 (
    .in1(4'b0010), .out(ALUSel), .sel(and_24_out));  // open: in0
  and and_24 (and_24_out, and_11_out, RType);
  Multiplexer #(.width(4), .enable("false")) multiplexer_12 (
    .in1(4'b1001), .out(ALUSel), .sel(and_25_out));  // open: in0
  and and_25 (and_25_out, and_12_out, RType);
  Multiplexer #(.width(4), .enable("false")) multiplexer_13 (
    .in1(4'b0001), .out(ALUSel), .sel(and_26_out));  // open: in0
  and and_26 (and_26_out, and_13_out, RType);
  Comparator #(.width(7), .mode("unsigned")) comparator_27 (
    .a(OPCODE), .b(7'b1100111), .eq(comparator_27_eq));  // open: gt, lt
  Comparator #(.width(7), .mode("unsigned")) comparator_28 (
    .a(OPCODE), .b(7'b0100011), .eq(comparator_28_eq));  // open: gt, lt
  Comparator #(.width(7), .mode("unsigned")) comparator_29 (
    .a(OPCODE), .b({7{1'b0}}), .eq(comparator_29_eq));  // open: gt, lt
  Multiplexer #(.width(3), .enable("false")) multiplexer_14 (.in1(3'b001), .out(ImmSel), .sel(IType));  // open: in0
  Multiplexer #(.width(3), .enable("false")) multiplexer_15 (
    .in1(3'b001), .out(ImmSel), .sel(comparator_27_eq));  // open: in0
  Multiplexer #(.width(3), .enable("false")) multiplexer_16 (
    .in1(3'b010), .out(ImmSel), .sel(comparator_28_eq));  // open: in0
  Multiplexer #(.enable("false")) multiplexer_17 (.in1(1'b1), .out(PCSel), .sel(comparator_29_eq));  // open: in0
  Comparator #(.width(7), .mode("unsigned")) comparator_30 (.a(OPCODE), .b(7'b0110011), .eq(RType));  // open: gt, lt
  Multiplexer #(.enable("false")) multiplexer_18 (.in1(1'b0), .out(BSel), .sel(RType));  // open: in0
  Multiplexer #(.width(2), .enable("false")) multiplexer_19 (.in1(2'b00), .out(WBSel), .sel(RType));  // open: in0
  Multiplexer #(.enable("false")) multiplexer_20 (.in1(1'b1), .out(RegWEn), .sel(RType));  // open: in0
  Multiplexer #(.enable("false")) multiplexer_21 (.in1(1'b1), .out(ASel), .sel(RType));  // open: in0
  Multiplexer #(.enable("false")) multiplexer_22 (.in1(1'b0), .out(MemRW), .sel(RType));  // open: in0
  Multiplexer #(.enable("false")) multiplexer_23 (.in1(1'b1), .out(PCSel), .sel(RType));  // open: in0
  Multiplexer #(.enable("false")) multiplexer_24 (.in1(1'b1), .out(BSel), .sel(jal));  // open: in0
  Multiplexer #(.width(2), .enable("false")) multiplexer_25 (.in1(2'b10), .out(WBSel), .sel(jal));  // open: in0
  Multiplexer #(.enable("false")) multiplexer_26 (.in1(1'b1), .out(RegWEn), .sel(jal));  // open: in0
  Multiplexer #(.enable("false")) multiplexer_27 (.in1(1'b0), .out(ASel), .sel(jal));  // open: in0
  Multiplexer #(.enable("false")) multiplexer_28 (.in1(1'b0), .out(MemRW), .sel(jal));  // open: in0
  Multiplexer #(.enable("false")) multiplexer_29 (.in1(1'b0), .out(PCSel), .sel(jal));  // open: in0
  Comparator #(.width(7), .mode("unsigned")) comparator_31 (
    .a(OPCODE), .b(7'b1101111), .eq(comparator_31_eq));  // open: gt, lt
  Multiplexer #(.width(4), .enable("false")) multiplexer_30 (.in1(4'b0000), .out(ALUSel), .sel(jal));  // open: in0
  Multiplexer #(.width(3), .enable("false")) multiplexer_31 (.in1(3'b011), .out(ImmSel), .sel(BType));  // open: in0
  Comparator #(.width(7), .mode("unsigned")) comparator_32 (
    .a(OPCODE), .b(7'b0110111), .eq(comparator_32_eq));  // open: gt, lt
  Comparator #(.width(7), .mode("unsigned")) comparator_33 (
    .a(OPCODE), .b(7'b1101111), .eq(comparator_33_eq));  // open: gt, lt
  Comparator #(.width(7), .mode("unsigned")) comparator_34 (
    .a(OPCODE), .b(7'b0000011), .eq(comparator_34_eq));  // open: gt, lt
  Multiplexer #(.enable("false")) multiplexer_32 (.in1(1'b1), .out(jal), .sel(comparator_31_eq));  // open: in0
  Multiplexer #(.width(3), .enable("false")) multiplexer_33 (
    .in1(3'b100), .out(ImmSel), .sel(comparator_32_eq));  // open: in0
  Multiplexer #(.width(3), .enable("false")) multiplexer_34 (
    .in1(3'b101), .out(ImmSel), .sel(comparator_33_eq));  // open: in0
  Multiplexer #(.width(3), .enable("false")) multiplexer_35 (
    .in1(3'b001), .out(ImmSel), .sel(comparator_34_eq));  // open: in0
  Multiplexer #(.width(4), .enable("false")) multiplexer_36 (.in1(4'b0000), .out(ALUSel), .sel(jalr));  // open: in0
  Multiplexer #(.enable("false")) multiplexer_37 (.in1(1'b1), .out(BSel), .sel(jalr));  // open: in0
  Multiplexer #(.width(2), .enable("false")) multiplexer_38 (.in1(2'b10), .out(WBSel), .sel(jalr));  // open: in0
  Multiplexer #(.enable("false")) multiplexer_39 (.in1(1'b1), .out(RegWEn), .sel(jalr));  // open: in0
  Multiplexer #(.enable("false")) multiplexer_40 (.in1(1'b1), .out(ASel), .sel(jalr));  // open: in0
  Multiplexer #(.enable("false")) multiplexer_41 (.in1(1'b0), .out(MemRW), .sel(jalr));  // open: in0
  Multiplexer #(.enable("false")) multiplexer_42 (.in1(1'b0), .out(PCSel), .sel(jalr));  // open: in0
  Comparator #(.width(3), .mode("unsigned")) comparator_35 (
    .a(FUNCT3), .b(3'b000), .eq(comparator_35_eq));  // open: gt, lt
  and and_27 (and_27_out, comparator_35_eq, comparator_36_eq);
  Comparator #(.width(7), .mode("unsigned")) comparator_36 (
    .a(OPCODE), .b(7'b0010011), .eq(comparator_36_eq));  // open: gt, lt
  Comparator #(.width(3), .mode("unsigned")) comparator_37 (
    .a(FUNCT3), .b(3'b001), .eq(comparator_37_eq));  // open: gt, lt
  and and_28 (and_28_out, comparator_37_eq, comparator_38_eq);
  Comparator #(.width(7), .mode("unsigned")) comparator_38 (
    .a(OPCODE), .b(7'b0010011), .eq(comparator_38_eq));  // open: gt, lt
  Comparator #(.width(7), .mode("unsigned")) comparator_39 (
    .a(FUNCT7), .b({7{1'b0}}), .eq(comparator_39_eq));  // open: gt, lt
  Comparator #(.width(3), .mode("unsigned")) comparator_40 (
    .a(FUNCT3), .b(3'b010), .eq(comparator_40_eq));  // open: gt, lt
  and and_29 (and_29_out, comparator_40_eq, comparator_41_eq);
  Comparator #(.width(7), .mode("unsigned")) comparator_41 (
    .a(OPCODE), .b(7'b0010011), .eq(comparator_41_eq));  // open: gt, lt
  Comparator #(.width(3), .mode("unsigned")) comparator_42 (
    .a(FUNCT3), .b(3'b100), .eq(comparator_42_eq));  // open: gt, lt
  and and_30 (and_30_out, comparator_42_eq, comparator_43_eq);
  Comparator #(.width(7), .mode("unsigned")) comparator_43 (
    .a(OPCODE), .b(7'b0010011), .eq(comparator_43_eq));  // open: gt, lt
  Comparator #(.width(3), .mode("unsigned")) comparator_44 (
    .a(FUNCT3), .b(3'b101), .eq(comparator_44_eq));  // open: gt, lt
  and and_31 (and_31_out, comparator_44_eq, comparator_45_eq);
  Comparator #(.width(7), .mode("unsigned")) comparator_45 (
    .a(OPCODE), .b(7'b0010011), .eq(comparator_45_eq));  // open: gt, lt
  Comparator #(.width(7), .mode("unsigned")) comparator_46 (
    .a(FUNCT7), .b({7{1'b0}}), .eq(comparator_46_eq));  // open: gt, lt
  Comparator #(.width(3), .mode("unsigned")) comparator_47 (
    .a(FUNCT3), .b(3'b101), .eq(comparator_47_eq));  // open: gt, lt
  and and_32 (and_32_out, comparator_47_eq, comparator_48_eq);
  Comparator #(.width(7), .mode("unsigned")) comparator_48 (
    .a(OPCODE), .b(7'b0010011), .eq(comparator_48_eq));  // open: gt, lt
  Comparator #(.width(7), .mode("unsigned")) comparator_49 (
    .a(FUNCT7), .b(7'b0100000), .eq(comparator_49_eq));  // open: gt, lt
  Comparator #(.width(3), .mode("unsigned")) comparator_50 (
    .a(FUNCT3), .b(3'b110), .eq(comparator_50_eq));  // open: gt, lt
  and and_33 (and_33_out, comparator_50_eq, comparator_51_eq);
  Comparator #(.width(7), .mode("unsigned")) comparator_51 (
    .a(OPCODE), .b(7'b0010011), .eq(comparator_51_eq));  // open: gt, lt
  Comparator #(.width(3), .mode("unsigned")) comparator_52 (
    .a(FUNCT3), .b(3'b111), .eq(comparator_52_eq));  // open: gt, lt
  and and_34 (and_34_out, comparator_52_eq, comparator_53_eq);
  Comparator #(.width(7), .mode("unsigned")) comparator_53 (
    .a(OPCODE), .b(7'b0010011), .eq(comparator_53_eq));  // open: gt, lt
  Multiplexer #(.enable("false")) multiplexer_43 (.in1(1'b1), .out(jalr), .sel(comparator_54_eq));  // open: in0
  Comparator #(.width(7), .mode("unsigned")) comparator_54 (
    .a(OPCODE), .b(7'b1100111), .eq(comparator_54_eq));  // open: gt, lt
  Multiplexer #(.width(4), .enable("false")) multiplexer_44 (
    .in1(4'b0000), .out(ALUSel), .sel(and_27_out));  // open: in0
  and and_35 (and_35_out, and_28_out, comparator_39_eq);
  Multiplexer #(.width(4), .enable("false")) multiplexer_45 (
    .in1(4'b0111), .out(ALUSel), .sel(and_29_out));  // open: in0
  Multiplexer #(.width(4), .enable("false")) multiplexer_46 (
    .in1(4'b0011), .out(ALUSel), .sel(and_30_out));  // open: in0
  and and_36 (and_36_out, and_31_out, comparator_46_eq);
  and and_37 (and_37_out, and_32_out, comparator_49_eq);
  Multiplexer #(.width(4), .enable("false")) multiplexer_47 (
    .in1(4'b0010), .out(ALUSel), .sel(and_33_out));  // open: in0
  Multiplexer #(.width(4), .enable("false")) multiplexer_48 (
    .in1(4'b0001), .out(ALUSel), .sel(and_34_out));  // open: in0
  Multiplexer #(.width(4), .enable("false")) multiplexer_49 (
    .in1(4'b0110), .out(ALUSel), .sel(and_35_out));  // open: in0
  Multiplexer #(.width(4), .enable("false")) multiplexer_50 (
    .in1(4'b0100), .out(ALUSel), .sel(and_36_out));  // open: in0
  Multiplexer #(.width(4), .enable("false")) multiplexer_51 (
    .in1(4'b0101), .out(ALUSel), .sel(and_37_out));  // open: in0
  Multiplexer #(.width(2), .enable("false")) multiplexer_52 (.in1(2'b01), .out(WBSel), .sel(lui));  // open: in0
  Multiplexer #(.enable("false")) multiplexer_53 (.in1(1'b1), .out(RegWEn), .sel(lui));  // open: in0
  Multiplexer #(.enable("false")) multiplexer_54 (.in1(1'b0), .out(MemRW), .sel(lui));  // open: in0
  Multiplexer #(.enable("false")) multiplexer_55 (.in1(1'b1), .out(PCSel), .sel(lui));  // open: in0
  Multiplexer #(.enable("false")) multiplexer_56 (.in0(1'b0), .in1(1'b1), .out(UType), .sel(lui));
  Multiplexer #(.enable("false")) multiplexer_57 (.in0(1'b0), .in1(1'b1), .out(lui), .sel(comparator_55_eq));
  Comparator #(.width(7), .mode("unsigned")) comparator_55 (
    .a(OPCODE), .b(7'b0110111), .eq(comparator_55_eq));  // open: gt, lt
  Multiplexer #(.enable("false")) multiplexer_58 (.in1(1'b1), .out(BSel), .sel(IType));  // open: in0
  Multiplexer #(.width(2), .enable("false")) multiplexer_59 (.in1(2'b00), .out(WBSel), .sel(IType));  // open: in0
  Multiplexer #(.enable("false")) multiplexer_60 (.in1(1'b1), .out(RegWEn), .sel(IType));  // open: in0
  Multiplexer #(.enable("false")) multiplexer_61 (.in1(1'b1), .out(ASel), .sel(IType));  // open: in0
  Multiplexer #(.enable("false")) multiplexer_62 (.in1(1'b0), .out(MemRW), .sel(IType));  // open: in0
  Multiplexer #(.enable("false")) multiplexer_63 (.in1(1'b1), .out(PCSel), .sel(IType));  // open: in0
  Comparator #(.width(7), .mode("unsigned")) comparator_56 (.a(OPCODE), .b(7'b0010011), .eq(IType));  // open: gt, lt
  Comparator #(.width(3), .mode("unsigned")) comparator_57 (
    .a(FUNCT3), .b(3'b000), .eq(comparator_57_eq));  // open: gt, lt
  Comparator #(.width(3), .mode("unsigned")) comparator_58 (
    .a(FUNCT3), .b(3'b000), .eq(comparator_58_eq));  // open: gt, lt
  Comparator #(.width(3), .mode("unsigned")) comparator_59 (
    .a(FUNCT3), .b(3'b001), .eq(comparator_59_eq));  // open: gt, lt
  Comparator #(.width(3), .mode("unsigned")) comparator_60 (
    .a(FUNCT3), .b(3'b001), .eq(comparator_60_eq));  // open: gt, lt
  Comparator #(.width(3), .mode("unsigned")) comparator_61 (
    .a(FUNCT3), .b(3'b100), .eq(comparator_61_eq));  // open: gt, lt
  Comparator #(.width(3), .mode("unsigned")) comparator_62 (
    .a(FUNCT3), .b(3'b100), .eq(comparator_62_eq));  // open: gt, lt
  Comparator #(.width(3), .mode("unsigned")) comparator_63 (
    .a(FUNCT3), .b(3'b110), .eq(comparator_63_eq));  // open: gt, lt
  Comparator #(.width(3), .mode("unsigned")) comparator_64 (
    .a(FUNCT3), .b(3'b110), .eq(comparator_64_eq));  // open: gt, lt
  Comparator #(.width(3), .mode("unsigned")) comparator_65 (
    .a(FUNCT3), .b(3'b100), .eq(comparator_65_eq));  // open: gt, lt
  Comparator #(.width(3), .mode("unsigned")) comparator_66 (
    .a(FUNCT3), .b(3'b110), .eq(comparator_66_eq));  // open: gt, lt
  and and_38 (and_38_out, BType, comparator_57_eq);
  and and_39 (and_39_out, BType, comparator_58_eq);
  not not_1 (not_1_out, BrEq);
  and and_40 (and_40_out, BType, comparator_59_eq);
  not not_2 (not_2_out, BrEq);
  and and_41 (and_41_out, BType, comparator_60_eq);
  and and_42 (and_42_out, BType, comparator_61_eq);
  and and_43 (and_43_out, BType, comparator_62_eq);
  not not_3 (not_3_out, BrLt);
  and and_44 (and_44_out, BType, comparator_63_eq);
  and and_45 (and_45_out, BType, comparator_64_eq);
  not not_4 (not_4_out, BrLt);
  and and_46 (and_46_out, BType, comparator_65_eq);
  and and_47 (and_47_out, BType, comparator_66_eq);
  Multiplexer #(.enable("false")) multiplexer_64 (.in1(1'b0), .out(PCSel), .sel(and_48_out));  // open: in0
  and and_48 (and_48_out, and_38_out, BrEq);
  Multiplexer #(.enable("false")) multiplexer_65 (.in1(1'b1), .out(PCSel), .sel(and_49_out));  // open: in0
  and and_49 (and_49_out, and_39_out, not_1_out);
  Multiplexer #(.enable("false")) multiplexer_66 (.in1(1'b0), .out(PCSel), .sel(and_50_out));  // open: in0
  and and_50 (and_50_out, and_40_out, not_2_out);
  Multiplexer #(.enable("false")) multiplexer_67 (.in1(1'b1), .out(PCSel), .sel(and_51_out));  // open: in0
  and and_51 (and_51_out, and_41_out, BrEq);
  Multiplexer #(.enable("false")) multiplexer_68 (.in1(1'b0), .out(PCSel), .sel(and_52_out));  // open: in0
  and and_52 (and_52_out, and_42_out, BrLt);
  Multiplexer #(.enable("false")) multiplexer_69 (.in1(1'b1), .out(PCSel), .sel(and_53_out));  // open: in0
  and and_53 (and_53_out, and_43_out, not_3_out);
  Multiplexer #(.enable("false")) multiplexer_70 (.in1(1'b0), .out(PCSel), .sel(and_54_out));  // open: in0
  and and_54 (and_54_out, and_44_out, BrLt);
  Multiplexer #(.enable("false")) multiplexer_71 (.in1(1'b1), .out(PCSel), .sel(and_55_out));  // open: in0
  and and_55 (and_55_out, and_45_out, not_4_out);
  Multiplexer #(.enable("false")) multiplexer_72 (.in1(1'b0), .out(BrUn), .sel(and_46_out));  // open: in0
  Multiplexer #(.enable("false")) multiplexer_73 (.in1(1'b1), .out(BrUn), .sel(and_47_out));  // open: in0
  Comparator #(.width(7), .mode("unsigned")) comparator_67 (.a(OPCODE), .b(7'b1100011), .eq(BType));  // open: gt, lt
  Multiplexer #(.enable("false")) multiplexer_74 (.in1(1'b1), .out(BSel), .sel(BType));  // open: in0
  Multiplexer #(.width(4), .enable("false")) multiplexer_75 (.in1(4'b0000), .out(ALUSel), .sel(BType));  // open: in0
  Multiplexer #(.enable("false")) multiplexer_76 (.in1(1'b0), .out(RegWEn), .sel(BType));  // open: in0
  Multiplexer #(.enable("false")) multiplexer_77 (.in1(1'b0), .out(ASel), .sel(BType));  // open: in0
  Multiplexer #(.enable("false")) multiplexer_78 (.in1(1'b0), .out(MemRW), .sel(BType));  // open: in0
  Comparator #(.width(3), .mode("unsigned")) comparator_68 (
    .a(FUNCT3), .b(3'b010), .eq(comparator_68_eq));  // open: gt, lt
  Comparator #(.width(7), .mode("unsigned")) comparator_69 (
    .a(OPCODE), .b(7'b0000011), .eq(comparator_69_eq));  // open: gt, lt
  Multiplexer #(.width(4), .enable("false")) multiplexer_79 (.in1(4'b0000), .out(ALUSel), .sel(lw));  // open: in0
  Multiplexer #(.enable("false")) multiplexer_80 (.in1(1'b1), .out(BSel), .sel(lw));  // open: in0
  Multiplexer #(.width(2), .enable("false")) multiplexer_81 (.in1(2'b01), .out(WBSel), .sel(lw));  // open: in0
  Multiplexer #(.enable("false")) multiplexer_82 (.in1(1'b1), .out(RegWEn), .sel(lw));  // open: in0
  Multiplexer #(.enable("false")) multiplexer_83 (.in1(1'b1), .out(ASel), .sel(lw));  // open: in0
  Multiplexer #(.enable("false")) multiplexer_84 (.in1(1'b0), .out(MemRW), .sel(lw));  // open: in0
  Multiplexer #(.enable("false")) multiplexer_85 (.in1(1'b1), .out(PCSel), .sel(lw));  // open: in0
  Multiplexer #(.width(2), .enable("false")) multiplexer_86 (.in1(2'b10), .out(DataSize), .sel(lw));  // open: in0
  Multiplexer #(.enable("false")) multiplexer_87 (.in1(1'b1), .out(lw), .sel(and_56_out));  // open: in0
  and and_56 (and_56_out, comparator_68_eq, comparator_69_eq);
  Comparator #(.width(3), .mode("unsigned")) comparator_70 (
    .a(FUNCT3), .b(3'b000), .eq(comparator_70_eq));  // open: gt, lt
  Comparator #(.width(7), .mode("unsigned")) comparator_71 (
    .a(OPCODE), .b(7'b0000011), .eq(comparator_71_eq));  // open: gt, lt
  Multiplexer #(.width(4), .enable("false")) multiplexer_88 (.in1(4'b0000), .out(ALUSel), .sel(lb));  // open: in0
  Multiplexer #(.enable("false")) multiplexer_89 (.in1(1'b1), .out(BSel), .sel(lb));  // open: in0
  Multiplexer #(.width(2), .enable("false")) multiplexer_90 (.in1(2'b01), .out(WBSel), .sel(lb));  // open: in0
  Multiplexer #(.enable("false")) multiplexer_91 (.in1(1'b1), .out(RegWEn), .sel(lb));  // open: in0
  Multiplexer #(.enable("false")) multiplexer_92 (.in1(1'b1), .out(ASel), .sel(lb));  // open: in0
  Multiplexer #(.enable("false")) multiplexer_93 (.in1(1'b0), .out(MemRW), .sel(lb));  // open: in0
  Multiplexer #(.enable("false")) multiplexer_94 (.in1(1'b1), .out(PCSel), .sel(lb));  // open: in0
  Multiplexer #(.width(2), .enable("false")) multiplexer_95 (.in1(2'b00), .out(DataSize), .sel(lb));  // open: in0
  Multiplexer #(.enable("false")) multiplexer_96 (.in1(1'b1), .out(lb), .sel(and_57_out));  // open: in0
  and and_57 (and_57_out, comparator_70_eq, comparator_71_eq);
  Multiplexer #(.width(4), .enable("false")) multiplexer_97 (.in1(4'b0000), .out(ALUSel), .sel(lh));  // open: in0
  Multiplexer #(.enable("false")) multiplexer_98 (.in1(1'b1), .out(BSel), .sel(lh));  // open: in0
  Multiplexer #(.width(2), .enable("false")) multiplexer_99 (.in1(2'b01), .out(WBSel), .sel(lh));  // open: in0
  Multiplexer #(.enable("false")) multiplexer_100 (.in1(1'b1), .out(RegWEn), .sel(lh));  // open: in0
  Multiplexer #(.enable("false")) multiplexer_101 (.in1(1'b1), .out(ASel), .sel(lh));  // open: in0
  Multiplexer #(.enable("false")) multiplexer_102 (.in1(1'b0), .out(MemRW), .sel(lh));  // open: in0
  Multiplexer #(.enable("false")) multiplexer_103 (.in1(1'b1), .out(PCSel), .sel(lh));  // open: in0
  Multiplexer #(.width(2), .enable("false")) multiplexer_104 (.in1(2'b01), .out(DataSize), .sel(lh));  // open: in0
  Comparator #(.width(3), .mode("unsigned")) comparator_72 (
    .a(FUNCT3), .b(3'b001), .eq(comparator_72_eq));  // open: gt, lt
  and and_58 (and_58_out, comparator_72_eq, comparator_73_eq);
  Comparator #(.width(7), .mode("unsigned")) comparator_73 (
    .a(OPCODE), .b(7'b0000011), .eq(comparator_73_eq));  // open: gt, lt
  Multiplexer #(.enable("false")) multiplexer_105 (.in1(1'b1), .out(lh), .sel(and_58_out));  // open: in0
  Multiplexer #(.width(4), .enable("false")) multiplexer_106 (.in1(4'b0000), .out(ALUSel), .sel(sw));  // open: in0
  Multiplexer #(.enable("false")) multiplexer_107 (.in1(1'b1), .out(BSel), .sel(sw));  // open: in0
  Multiplexer #(.width(2), .enable("false")) multiplexer_108 (.in1(2'b01), .out(WBSel), .sel(sw));  // open: in0
  Multiplexer #(.enable("false")) multiplexer_109 (.in1(1'b0), .out(RegWEn), .sel(sw));  // open: in0
  Multiplexer #(.enable("false")) multiplexer_110 (.in1(1'b1), .out(ASel), .sel(sw));  // open: in0
  Multiplexer #(.enable("false")) multiplexer_111 (.in1(1'b1), .out(MemRW), .sel(sw));  // open: in0
  Multiplexer #(.enable("false")) multiplexer_112 (.in1(1'b1), .out(PCSel), .sel(sw));  // open: in0
  Multiplexer #(.width(2), .enable("false")) multiplexer_113 (.in1(2'b10), .out(DataSize), .sel(sw));  // open: in0
  Comparator #(.width(3), .mode("unsigned")) comparator_74 (
    .a(FUNCT3), .b(3'b010), .eq(comparator_74_eq));  // open: gt, lt
  and and_59 (and_59_out, comparator_74_eq, comparator_75_eq);
  Comparator #(.width(7), .mode("unsigned")) comparator_75 (
    .a(OPCODE), .b(7'b0100011), .eq(comparator_75_eq));  // open: gt, lt
  Multiplexer #(.enable("false")) multiplexer_114 (.in1(1'b1), .out(sw), .sel(and_59_out));  // open: in0

  // Notes on the sheet:
  //   add
  //   mul
  //   sub
  //   sll
  //   mulh
  //   mulhu
  //   slt
  //   xor
  //   divu
  //   srl
  //   or
  //   remu
  //   and
  //   ALUSel for Rtype
  //   Other controls for Rtype
  //   ImmSel for any type
  //   jal
  //   addi
  //   slli
  //   slti
  //   xori
  //   srli
  //   srai
  //   ori
  //   andi
  //   ALUSel for Itype-exclude
  //   jalr
  //   lui
  //   Other controls for Itype-exclude
  //   beq
  //   bne
  //   blt
  //   bltu
  //   blt
  //   bltu
  //   PCSel for Btype
  //   BrUn for Btype
  //   Other controls for Btype
  //   lw
  //   lb
  //   lh
  //   sw
endmodule

module immgen (
  input  [31:0] INSTRUCTION,
  input  [2:0] IMMSEL,
  output [31:0] Immediate
);

  wire [31:0] bit_extender_1_out, bit_extender_2_out, bit_extender_3_out, bit_extender_4_out;

  assign bit_extender_1_out = {{20{INSTRUCTION[31]}}, INSTRUCTION[31:20]};  // Bit_Extender bit_extender_1
  assign bit_extender_2_out = {{20{INSTRUCTION[31]}}, {INSTRUCTION[31:25], INSTRUCTION[11:7]}};  // Bit_Extender bit_extender_2
  assign bit_extender_3_out = {{19{INSTRUCTION[31]}}, {INSTRUCTION[31], INSTRUCTION[7], INSTRUCTION[30:25], INSTRUCTION[11:8], 1'b0}};  // Bit_Extender bit_extender_3
  assign bit_extender_4_out = {{11{INSTRUCTION[31]}}, {INSTRUCTION[31], INSTRUCTION[19:12], INSTRUCTION[20], INSTRUCTION[30:21], 1'b0}};  // Bit_Extender bit_extender_4
  Multiplexer #(.select(3), .width(32), .enable("false")) multiplexer_1 (
    .in1(bit_extender_1_out), .in2(bit_extender_2_out), .in3(bit_extender_3_out),
    .in4({INSTRUCTION[31:12], {12{1'b0}}}), .in5(bit_extender_4_out), .out(Immediate), .sel(IMMSEL));  // open: in0, in6, in7

  // Other names for the same wires on the sheet: B[12:1] = {INSTRUCTION[31], INSTRUCTION[7], INSTRUCTION[30:25], INSTRUCTION[11:8]};
  //   rd[4:0] = INSTRUCTION[11:7]; S[11:0] = {INSTRUCTION[31:25], INSTRUCTION[11:7]}; opcode[6:0] = INSTRUCTION[6:0];
  //   I[11:0] = INSTRUCTION[31:20];
  //   J[20:1] = {INSTRUCTION[31], INSTRUCTION[19:12], INSTRUCTION[20], INSTRUCTION[30:21]};
  //   rs2[4:0] = INSTRUCTION[24:20]; U[31:12] = INSTRUCTION[31:12]; funct7[6:0] = INSTRUCTION[31:25];
  //   funct3[2:0] = INSTRUCTION[14:12]; rs1[4:0] = INSTRUCTION[19:15]
endmodule

// BrLt
module branch (
  input  [31:0] rs1,
  input  [31:0] rs2,
  input  in_3,
  output BrEq,
  output BrLt
);

  wire comparator_1_lt, comparator_2_lt;

  Comparator #(.width(32)) comparator_1 (.a(rs1), .b(rs2), .eq(BrEq), .lt(comparator_1_lt));  // open: gt
  Comparator #(.width(32), .mode("unsigned")) comparator_2 (.a(rs1), .b(rs2), .lt(comparator_2_lt));  // open: gt, eq
  Multiplexer #(.enable("false")) multiplexer_1 (.in0(comparator_1_lt), .in1(comparator_2_lt), .out(BrLt), .sel(in_3));

  // Other names for the same wires on the sheet: BrUn = in_3
endmodule

module memory (
  input  [31:0] Address,
  input  [31:0] DataIn,
  input  [1:0] DataSize,
  output [31:0] DataOut
);

  wire comparator_1_eq, comparator_2_eq, comparator_3_eq;
  wire [4:0] bit_extender_1_out, bit_extender_3_out, multiplier_1_out, multiplier_2_out;
  wire [7:0] shifter_2_out;
  wire [31:0] bit_extender_2_out, bit_extender_4_out, shifter_1_out;
  wire [31:8] shifter_2_out_2;

  Multiplexer #(.width(32), .enable("false")) multiplexer_1 (
    .in1(DataIn), .out(DataOut), .sel(comparator_1_eq));  // open: in0
  Comparator #(.width(2)) comparator_1 (.a(DataSize), .b(2'b10), .eq(comparator_1_eq));  // open: gt, lt
  assign bit_extender_1_out = {{4{Address[1]}}, Address[1]};  // Bit_Extender bit_extender_1
  Shifter #(.width(32), .shift("lr")) shifter_1 (.in(DataIn), .\dist (multiplier_1_out), .out(shifter_1_out));
  Multiplier #(.width(5)) multiplier_1 (
    .a(bit_extender_1_out), .b(5'b10000), .out(multiplier_1_out));  // open: cin, cout
  assign bit_extender_2_out = {{16{shifter_1_out[15]}}, shifter_1_out[15:0]};  // Bit_Extender bit_extender_2
  assign bit_extender_3_out = {{3{Address[1]}}, Address[1:0]};  // Bit_Extender bit_extender_3
  Multiplexer #(.width(32), .enable("false")) multiplexer_2 (
    .in1(bit_extender_2_out), .out(DataOut), .sel(comparator_2_eq));  // open: in0
  Comparator #(.width(2)) comparator_2 (.a(DataSize), .b(2'b01), .eq(comparator_2_eq));  // open: gt, lt
  Multiplier #(.width(5)) multiplier_2 (
    .a(bit_extender_3_out), .b(5'b01000), .out(multiplier_2_out));  // open: cin, cout
  Shifter #(.width(32), .shift("lr")) shifter_2 (
    .in(DataIn), .\dist (multiplier_2_out), .out({shifter_2_out_2, shifter_2_out}));
  assign bit_extender_4_out = {{24{shifter_2_out[7]}}, shifter_2_out};  // Bit_Extender bit_extender_4
  Comparator #(.width(2)) comparator_3 (.a(DataSize), .b(2'b00), .eq(comparator_3_eq));  // open: gt, lt
  Multiplexer #(.width(32), .enable("false")) multiplexer_3 (
    .in1(bit_extender_4_out), .out(DataOut), .sel(comparator_3_eq));  // open: in0
endmodule
