// Logisim project cpu.circ as structural Verilog: 4 circuits, main circuit main
module main (
  input  [31:0] INSTRUCTION,
  input  CLOCK,
  output [31:0] PROGRAM_COUNTER,
  output [31:0] ra,
  output [31:0] sp,
  output [31:0] t0,
  output [31:0] t1,
  output [31:0] t2,
  output [31:0] s0,
  output [31:0] s1,
  output [31:0] a0
);

  wire ASel, BrEq, BrLt, BrUn, BSel, MemRW, PCSel, RegWEn;
  wire [1:0] WBSel;
  wire [2:0] ImmSel;
  wire [3:0] ALUSel;
  wire [19:0] immgen_1_immediate;
  wire [31:0] adder_1_out, Arithmetic_Logic_Unit_result, bit_extender_1_out, DMEM_p5, multiplexer_1_out,
       multiplexer_2_out, multiplexer_3_out, multiplexer_4_out, RegFile_read_data_1, RegFile_read_data_2;

  Adder #(.width(32)) adder_1 (.a(PROGRAM_COUNTER), .b(32'h4), .out(adder_1_out));  // open: cin, cout
  Multiplexer #(.width(32), .enable("false")) multiplexer_1 (
    .in0(Arithmetic_Logic_Unit_result), .in1(adder_1_out), .out(multiplexer_1_out), .sel(PCSel));
  Register #(.width(32)) PC (.D(multiplexer_1_out), .clk(CLOCK), .Q(PROGRAM_COUNTER));  // open: en, clr
  control control_1 (
    .OPCODE(INSTRUCTION[6:0]), .FUNCT3(INSTRUCTION[14:12]), .FUNCT7(INSTRUCTION[31:25]), .BrEq(BrEq),
    .BrLt(BrLt), .ALUSel(ALUSel), .ImmSel(ImmSel), .RegWEn(RegWEn), .ASel(ASel), .BSel(BSel), .BrUn(BrUn),
    .WBSel(WBSel), .MemRW(MemRW), .PCSel(PCSel));
  immgen immgen_1 (.INSTRUCTION(INSTRUCTION), .IMMSEL(ImmSel), .Immediate(immgen_1_immediate));
  regfile_main RegFile (
    .rs2(INSTRUCTION[24:20]), .rd(INSTRUCTION[11:7]), .Read_Data_1(RegFile_read_data_1),
    .Read_Data_2(RegFile_read_data_2), .ra(ra), .sp(sp), .t0(t0), .t1(t1), .t2(t2), .s0(s0), .s1(s1),
    .a0(a0), .rs1(INSTRUCTION[19:15]), .Write_Data(multiplexer_4_out), .RegWEn(RegWEn), .clk(CLOCK));
  assign bit_extender_1_out = {{12{immgen_1_immediate[19]}}, immgen_1_immediate};  // Bit_Extender bit_extender_1
  Multiplexer #(.width(32), .enable("false")) multiplexer_2 (
    .in0(PROGRAM_COUNTER), .in1(RegFile_read_data_1), .out(multiplexer_2_out), .sel(ASel));
  branch branch_1 (.rs1(RegFile_read_data_1), .rs2(RegFile_read_data_2), .in_3(BrUn), .BrEq(BrEq), .BrLt(BrLt));
  Multiplexer #(.width(32), .enable("false")) multiplexer_3 (
    .in0(RegFile_read_data_2), .in1(bit_extender_1_out), .out(multiplexer_3_out), .sel(BSel));
  alu Arithmetic_Logic_Unit (
    .B(multiplexer_3_out), .Result(Arithmetic_Logic_Unit_result), .A(multiplexer_2_out), .ALUSel(ALUSel));
  // mem_main DMEM: pin names not known; wires that end beside it: Arithmetic_Logic_Unit_result, RegFile_read_data_2, CLOCK, MemRW, DMEM_p5
  Multiplexer #(.select(2), .width(32), .enable("false")) multiplexer_4 (
    .in0(Arithmetic_Logic_Unit_result), .in1(DMEM_p5), .out(multiplexer_4_out), .sel(WBSel));  // open: in2, in3

  // Other names for the same wires on the sheet: clk = CLOCK; opcode[6:0] = INSTRUCTION[6:0];
  //   rd[4:0] = INSTRUCTION[11:7]; funct3[2:0] = INSTRUCTION[14:12]; rs1[4:0] = INSTRUCTION[19:15];
  //   rs2[4:0] = INSTRUCTION[24:20]; funct7[6:0] = INSTRUCTION[31:25]

  // Notes on the sheet:
  //   Output
  //   IMEM (do **NOT** move this)
  //   Inputs
  //   Inputs/Outputs for testing. Do **NOT** move these.
endmodule

module control (
  input  [6:0] OPCODE,
  input  [2:0] FUNCT3,
  input  [6:0] FUNCT7,
  input  BrEq,
  input  BrLt,
  output [3:0] ALUSel,
  output [2:0] ImmSel,
  output RegWEn,
  output ASel,
  output BSel,
  output BrUn,
  output [1:0] WBSel,
  output MemRW,
  output PCSel
);

  wire and_1_out, and_2_out, and_3_out, and_4_out, and_5_out, and_6_out, and_7_out, and_8_out, and_9_out,
       and_10_out, and_11_out, and_12_out, and_13_out, and_14_out, and_16_out, and_17_out, and_18_out,
       and_19_out, and_20_out, and_21_out, and_22_out, and_23_out, and_24_out, and_25_out, and_26_out,
       and_27_out, and_28_out, and_29_out, and_30_out, and_31_out, and_32_out, and_33_out, and_34_out,
       and_35_out, and_36_out, and_37_out, and_38_out, and_39_out, and_40_out, and_41_out, and_42_out,
       and_43_out, and_44_out, and_45_out, and_46_out, and_47_out, and_48_out, and_49_out, and_50_out,
       and_51_out, and_52_out, and_53_out, and_54_out, and_55_out, and_56_out, and_57_out, and_58_out,
       and_59_out, BType, comparator_1_eq, comparator_2_eq, comparator_3_eq, comparator_4_eq,
       comparator_5_eq, comparator_6_eq, comparator_7_eq, comparator_8_eq, comparator_9_eq, comparator_10_eq,
       comparator_11_eq, comparator_12_eq, comparator_13_eq, comparator_14_eq, comparator_15_eq,
       comparator_16_eq, comparator_17_eq, comparator_18_eq, comparator_19_eq, comparator_20_eq,
       comparator_21_eq, comparator_22_eq, comparator_23_eq, comparator_24_eq, comparator_25_eq,
       comparator_26_eq, comparator_27_eq, comparator_28_eq, comparator_29_eq, comparator_31_eq,
       comparator_32_eq, comparator_33_eq, comparator_34_eq, comparator_35_eq, comparator_36_eq,
       comparator_37_eq, comparator_38_eq, comparator_39_eq, comparator_40_eq, comparator_41_eq,
       comparator_42_eq, comparator_43_eq, comparator_44_eq, comparator_45_eq, comparator_46_eq,
       comparator_47_eq, comparator_48_eq, comparator_49_eq, comparator_50_eq, comparator_51_eq,
       comparator_52_eq, comparator_53_eq, comparator_54_eq, comparator_55_eq, comparator_56_eq,
       comparator_57_eq, comparator_58_eq, comparator_59_eq, comparator_60_eq, comparator_61_eq,
       comparator_62_eq, comparator_64_eq, comparator_65_eq, comparator_66_eq, comparator_67_eq,
       comparator_68_eq, comparator_69_eq, comparator_70_eq, comparator_71_eq, IType, lb, lw,
       multiplexer_2_p2, not_2_out, not_3_out, not_4_out, not_5_out, or_1_out, or_2_out, RType;
  wire [3:0] bit_extender_1_out, ImmSig, not_1_out, xor_1_out;

  Comparator #(.width(3), .mode("unsigned")) comparator_1 (
    .a(FUNCT3), .b(3'b000), .eq(comparator_1_eq));  // open: gt, lt
  Comparator #(.width(7), .mode("unsigned")) comparator_2 (
    .a(FUNCT7), .b({7{1'b0}}), .eq(comparator_2_eq));  // open: gt, lt
  Comparator #(.width(3), .mode("unsigned")) comparator_3 (
    .a(FUNCT3), .b(3'b000), .eq(comparator_3_eq));  // open: gt, lt
  Comparator #(.width(7), .mode("unsigned")) comparator_4 (
    .a(FUNCT7), .b(7'b0000001), .eq(comparator_4_eq));  // open: gt, lt
  Comparator #(.width(3), .mode("unsigned")) comparator_5 (
    .a(FUNCT3), .b(3'b000), .eq(comparator_5_eq));  // open: gt, lt
  Comparator #(.width(7), .mode("unsigned")) comparator_6 (
    .a(FUNCT7), .b(7'b0100000), .eq(comparator_6_eq));  // open: gt, lt
  Comparator #(.width(3), .mode("unsigned")) comparator_7 (
    .a(FUNCT3), .b(3'b001), .eq(comparator_7_eq));  // open: gt, lt
  Comparator #(.width(7), .mode("unsigned")) comparator_8 (
    .a(FUNCT7), .b({7{1'b0}}), .eq(comparator_8_eq));  // open: gt, lt
  Comparator #(.width(3), .mode("unsigned")) comparator_9 (
    .a(FUNCT3), .b(3'b001), .eq(comparator_9_eq));  // open: gt, lt
  Comparator #(.width(7), .mode("unsigned")) comparator_10 (
    .a(FUNCT7), .b(7'b0000001), .eq(comparator_10_eq));  // open: gt, lt
  Comparator #(.width(3), .mode("unsigned")) comparator_11 (
    .a(FUNCT3), .b(3'b011), .eq(comparator_11_eq));  // open: gt, lt
  Comparator #(.width(7), .mode("unsigned")) comparator_12 (
    .a(FUNCT7), .b(7'b0000001), .eq(comparator_12_eq));  // open: gt, lt
  Comparator #(.width(3), .mode("unsigned")) comparator_13 (
    .a(FUNCT3), .b(3'b010), .eq(comparator_13_eq));  // open: gt, lt
  Comparator #(.width(7), .mode("unsigned")) comparator_14 (
    .a(FUNCT7), .b({7{1'b0}}), .eq(comparator_14_eq));  // open: gt, lt
  Comparator #(.width(3), .mode("unsigned")) comparator_15 (
    .a(FUNCT3), .b(3'b100), .eq(comparator_15_eq));  // open: gt, lt
  Comparator #(.width(7), .mode("unsigned")) comparator_16 (
    .a(FUNCT7), .b({7{1'b0}}), .eq(comparator_16_eq));  // open: gt, lt
  Comparator #(.width(3), .mode("unsigned")) comparator_17 (
    .a(FUNCT3), .b(3'b101), .eq(comparator_17_eq));  // open: gt, lt
  Comparator #(.width(7), .mode("unsigned")) comparator_18 (
    .a(FUNCT7), .b(7'b0000001), .eq(comparator_18_eq));  // open: gt, lt
  Comparator #(.width(3), .mode("unsigned")) comparator_19 (
    .a(FUNCT3), .b(3'b101), .eq(comparator_19_eq));  // open: gt, lt
  Comparator #(.width(7), .mode("unsigned")) comparator_20 (
    .a(FUNCT7), .b({7{1'b0}}), .eq(comparator_20_eq));  // open: gt, lt
  Comparator #(.width(3), .mode("unsigned")) comparator_21 (
    .a(FUNCT3), .b(3'b110), .eq(comparator_21_eq));  // open: gt, lt
  Comparator #(.width(7), .mode("unsigned")) comparator_22 (
    .a(FUNCT7), .b({7{1'b0}}), .eq(comparator_22_eq));  // open: gt, lt
  Comparator #(.width(3), .mode("unsigned")) comparator_23 (
    .a(FUNCT3), .b(3'b111), .eq(comparator_23_eq));  // open: gt, lt
  Comparator #(.width(7), .mode("unsigned")) comparator_24 (
    .a(FUNCT7), .b(7'b0000001), .eq(comparator_24_eq));  // open: gt, lt
  Comparator #(.width(3), .mode("unsigned")) comparator_25 (
    .a(FUNCT3), .b(3'b111), .eq(comparator_25_eq));  // open: gt, lt
  Comparator #(.width(7), .mode("unsigned")) comparator_26 (
    .a(FUNCT7), .b({7{1'b0}}), .eq(comparator_26_eq));  // open: gt, lt
  and and_1 (and_1_out, comparator_1_eq, comparator_2_eq);
  and and_2 (and_2_out, comparator_3_eq, comparator_4_eq);
  and and_3 (and_3_out, comparator_5_eq, comparator_6_eq);
  and and_4 (and_4_out, comparator_7_eq, comparator_8_eq);
  and and_5 (and_5_out, comparator_9_eq, comparator_10_eq);
  and and_6 (and_6_out, comparator_11_eq, comparator_12_eq);
  and and_7 (and_7_out, comparator_13_eq, comparator_14_eq);
  and and_8 (and_8_out, comparator_15_eq, comparator_16_eq);
  and and_9 (and_9_out, comparator_17_eq, comparator_18_eq);
  and and_10 (and_10_out, comparator_19_eq, comparator_20_eq);
  and and_11 (and_11_out, comparator_21_eq, comparator_22_eq);
  and and_12 (and_12_out, comparator_23_eq, comparator_24_eq);
  and and_13 (and_13_out, comparator_25_eq, comparator_26_eq);
  Multiplexer #(.width(4), .enable("false")) multiplexer_1 (
    .in1(4'b0000), .out(ALUSel), .sel(and_14_out));  // open: in0
  and and_14 (and_14_out, and_1_out, RType);
  // Multiplexer #(.width(4), .enable("false")) multiplexer_2: pin names not known; wires that end beside it: 4'b1010, multiplexer_2_p2, ALUSel
  and and_15 (multiplexer_2_p2, and_2_out, RType);
  Multiplexer #(.width(4), .enable("false")) multiplexer_3 (
    .in1(4'b1100), .out(ALUSel), .sel(and_16_out));  // open: in0
  and and_16 (and_16_out, and_3_out, RType);
  Multiplexer #(.width(4), .enable("false")) multiplexer_4 (
    .in1(4'b0110), .out(ALUSel), .sel(and_17_out));  // open: in0
  and and_17 (and_17_out, and_4_out, RType);
  Multiplexer #(.width(4), .enable("false")) multiplexer_5 (
    .in1(4'b1110), .out(ALUSel), .sel(and_18_out));  // open: in0
  and and_18 (and_18_out, and_5_out, RType);
  Multiplexer #(.width(4), .enable("false")) multiplexer_6 (
    .in1(4'b1011), .out(ALUSel), .sel(and_19_out));  // open: in0
  and and_19 (and_19_out, and_6_out, RType);
  Multiplexer #(.width(4), .enable("false")) multiplexer_7 (
    .in1(4'b0111), .out(ALUSel), .sel(and_20_out));  // open: in0
  and and_20 (and_20_out, and_7_out, RType);
  Multiplexer #(.width(4), .enable("false")) multiplexer_8 (
    .in1(4'b0011), .out(ALUSel), .sel(and_21_out));  // open: in0
  and and_21 (and_21_out, and_8_out, RType);
  Multiplexer #(.width(4), .enable("false")) multiplexer_9 (
    .in1(4'b1000), .out(ALUSel), .sel(and_22_out));  // open: in0
  and and_22 (and_22_out, and_9_out, RType);
  Multiplexer #(.width(4), .enable("false")) multiplexer_10 (
    .in1(4'b0100), .out(ALUSel), .sel(and_23_out));  // open: in0
  and and_23 (and_23_out, and_10_out, RType);
  Multiplexer #(.width(4), .enable("false")) multiplexer_11 (
    .in1(4'b0010), .out(ALUSel), .sel(and_24_out));  // open: in0
  and and_24 (and_24_out, and_11_out, RType);
  Multiplexer #(.width(4), .enable("false")) multiplexer_12 (
    .in1(4'b1001), .out(ALUSel), .sel(and_25_out));  // open: in0
  and and_25 (and_25_out, and_12_out, RType);
  Multiplexer #(.width(4), .enable("false")) multiplexer_13 (
    .in1(4'b0001), .out(ALUSel), .sel(and_26_out));  // open: in0
  and and_26 (and_26_out, and_13_out, RType);
  assign xor_1_out = bit_extender_1_out ^ OPCODE[3:0];  // XOR_Gate xor_1, 4 bits wide
  Comparator #(.width(3), .mode("unsigned")) comparator_27 (
    .a(OPCODE[6:4]), .b(3'b011), .eq(comparator_27_eq));  // open: gt, lt
  Comparator #(.width(3), .mode("unsigned")) comparator_28 (
    .a(OPCODE[6:4]), .b(3'b110), .eq(comparator_28_eq));  // open: gt, lt
  assign bit_extender_1_out = {{1{1'b0}}, OPCODE[6:4]};  // Bit_Extender bit_extender_1
  Multiplexer #(.width(4), .enable("false")) multiplexer_14 (
    .in0(bit_extender_1_out), .in1(not_1_out), .out(ImmSig), .sel(or_1_out));
  assign not_1_out = ~xor_1_out;  // NOT_Gate not_1, 4 bits wide
  or or_1 (or_1_out, comparator_27_eq, comparator_28_eq);
  Multiplexer #(.enable("false")) multiplexer_15 (.in1(1'b1), .out(PCSel), .sel(comparator_29_eq));  // open: in0
  Comparator #(.width(7), .mode("unsigned")) comparator_29 (
    .a(OPCODE), .b({7{1'b0}}), .eq(comparator_29_eq));  // open: gt, lt
  Comparator #(.width(7), .mode("unsigned")) comparator_30 (.a(OPCODE), .b(7'b0110011), .eq(RType));  // open: gt, lt
  Multiplexer #(.enable("false")) multiplexer_16 (.in1(1'b0), .out(BSel), .sel(RType));  // open: in0
  Multiplexer #(.width(2), .enable("false")) multiplexer_17 (.in1(2'b00), .out(WBSel), .sel(RType));  // open: in0
  Multiplexer #(.enable("false")) multiplexer_18 (.in1(1'b1), .out(RegWEn), .sel(RType));  // open: in0
  Multiplexer #(.enable("false")) multiplexer_19 (.in1(1'b1), .out(ASel), .sel(RType));  // open: in0
  Multiplexer #(.enable("false")) multiplexer_20 (.in1(1'b0), .out(MemRW), .sel(RType));  // open: in0
  Multiplexer #(.enable("false")) multiplexer_21 (.in1(1'b1), .out(PCSel), .sel(RType));  // open: in0
  Multiplexer #(.select(4), .width(3), .enable("false")) multiplexer_22 (
    .in0(3'b001), .in1(3'b001), .in2(3'b010), .in6(3'b101), .in10(3'b011), .in11(3'b100), .in14(3'b010),
    .out(ImmSel), .sel(ImmSig));  // open: in3, in4, in5, in7, in8, in9, in12, in13, in15
  Comparator #(.width(3), .mode("unsigned")) comparator_31 (
    .a(FUNCT3), .b(3'b000), .eq(comparator_31_eq));  // open: gt, lt
  and and_27 (and_27_out, comparator_31_eq, comparator_32_eq);
  Comparator #(.width(7), .mode("unsigned")) comparator_32 (
    .a(OPCODE), .b(7'b0010011), .eq(comparator_32_eq));  // open: gt, lt
  Comparator #(.width(3), .mode("unsigned")) comparator_33 (
    .a(FUNCT3), .b(3'b001), .eq(comparator_33_eq));  // open: gt, lt
  and and_28 (and_28_out, comparator_33_eq, comparator_34_eq);
  Comparator #(.width(7), .mode("unsigned")) comparator_34 (
    .a(OPCODE), .b(7'b0010011), .eq(comparator_34_eq));  // open: gt, lt
  Comparator #(.width(7), .mode("unsigned")) comparator_35 (
    .a(FUNCT7), .b({7{1'b0}}), .eq(comparator_35_eq));  // open: gt, lt
  Comparator #(.width(3), .mode("unsigned")) comparator_36 (
    .a(FUNCT3), .b(3'b010), .eq(comparator_36_eq));  // open: gt, lt
  and and_29 (and_29_out, comparator_36_eq, comparator_37_eq);
  Comparator #(.width(7), .mode("unsigned")) comparator_37 (
    .a(OPCODE), .b(7'b0010011), .eq(comparator_37_eq));  // open: gt, lt
  Comparator #(.width(3), .mode("unsigned")) comparator_38 (
    .a(FUNCT3), .b(3'b100), .eq(comparator_38_eq));  // open: gt, lt
  and and_30 (and_30_out, comparator_38_eq, comparator_39_eq);
  Comparator #(.width(7), .mode("unsigned")) comparator_39 (
    .a(OPCODE), .b(7'b0010011), .eq(comparator_39_eq));  // open: gt, lt
  Comparator #(.width(3), .mode("unsigned")) comparator_40 (
    .a(FUNCT3), .b(3'b101), .eq(comparator_40_eq));  // open: gt, lt
  and and_31 (and_31_out, comparator_40_eq, comparator_41_eq);
  Comparator #(.width(7), .mode("unsigned")) comparator_41 (
    .a(OPCODE), .b(7'b0010011), .eq(comparator_41_eq));  // open: gt, lt
  Comparator #(.width(7), .mode("unsigned")) comparator_42 (
    .a(FUNCT7), .b({7{1'b0}}), .eq(comparator_42_eq));  // open: gt, lt
  Comparator #(.width(3), .mode("unsigned")) comparator_43 (
    .a(FUNCT3), .b(3'b101), .eq(comparator_43_eq));  // open: gt, lt
  and and_32 (and_32_out, comparator_43_eq, comparator_44_eq);
  Comparator #(.width(7), .mode("unsigned")) comparator_44 (
    .a(OPCODE), .b(7'b0010011), .eq(comparator_44_eq));  // open: gt, lt
  Comparator #(.width(7), .mode("unsigned")) comparator_45 (
    .a(FUNCT7), .b(7'b0100000), .eq(comparator_45_eq));  // open: gt, lt
  Comparator #(.width(3), .mode("unsigned")) comparator_46 (
    .a(FUNCT3), .b(3'b110), .eq(comparator_46_eq));  // open: gt, lt
  and and_33 (and_33_out, comparator_46_eq, comparator_47_eq);
  Comparator #(.width(7), .mode("unsigned")) comparator_47 (
    .a(OPCODE), .b(7'b0010011), .eq(comparator_47_eq));  // open: gt, lt
  Comparator #(.width(3), .mode("unsigned")) comparator_48 (
    .a(FUNCT3), .b(3'b111), .eq(comparator_48_eq));  // open: gt, lt
  and and_34 (and_34_out, comparator_48_eq, comparator_49_eq);
  Comparator #(.width(7), .mode("unsigned")) comparator_49 (
    .a(OPCODE), .b(7'b0010011), .eq(comparator_49_eq));  // open: gt, lt
  Multiplexer #(.width(4), .enable("false")) multiplexer_23 (
    .in1(4'b0000), .out(ALUSel), .sel(and_27_out));  // open: in0
  and and_35 (and_35_out, and_28_out, comparator_35_eq);
  Multiplexer #(.width(4), .enable("false")) multiplexer_24 (
    .in1(4'b0111), .out(ALUSel), .sel(and_29_out));  // open: in0
  Multiplexer #(.width(4), .enable("false")) multiplexer_25 (
    .in1(4'b0011), .out(ALUSel), .sel(and_30_out));  // open: in0
  and and_36 (and_36_out, and_31_out, comparator_42_eq);
  and and_37 (and_37_out, and_32_out, comparator_45_eq);
  Multiplexer #(.width(4), .enable("false")) multiplexer_26 (
    .in1(4'b0010), .out(ALUSel), .sel(and_33_out));  // open: in0
  Multiplexer #(.width(4), .enable("false")) multiplexer_27 (
    .in1(4'b0001), .out(ALUSel), .sel(and_34_out));  // open: in0
  Multiplexer #(.width(4), .enable("false")) multiplexer_28 (
    .in1(4'b0110), .out(ALUSel), .sel(and_35_out));  // open: in0
  Multiplexer #(.width(4), .enable("false")) multiplexer_29 (
    .in1(4'b0100), .out(ALUSel), .sel(and_36_out));  // open: in0
  Multiplexer #(.width(4), .enable("false")) multiplexer_30 (
    .in1(4'b0101), .out(ALUSel), .sel(and_37_out));  // open: in0
  Multiplexer #(.enable("false")) multiplexer_31 (.in1(1'b1), .out(BSel), .sel(IType));  // open: in0
  Multiplexer #(.width(2), .enable("false")) multiplexer_32 (.in1(2'b00), .out(WBSel), .sel(IType));  // open: in0
  Multiplexer #(.enable("false")) multiplexer_33 (.in1(1'b1), .out(RegWEn), .sel(IType));  // open: in0
  Multiplexer #(.enable("false")) multiplexer_34 (.in1(1'b1), .out(ASel), .sel(IType));  // open: in0
  Multiplexer #(.enable("false")) multiplexer_35 (.in1(1'b0), .out(MemRW), .sel(IType));  // open: in0
  Multiplexer #(.enable("false")) multiplexer_36 (.in1(1'b1), .out(PCSel), .sel(IType));  // open: in0
  Comparator #(.width(7), .mode("unsigned")) comparator_50 (
    .a(OPCODE), .b(7'b0000011), .eq(comparator_50_eq));  // open: gt, lt
  Comparator #(.width(7), .mode("unsigned")) comparator_51 (
    .a(OPCODE), .b(7'b0010011), .eq(comparator_51_eq));  // open: gt, lt
  or or_2 (or_2_out, comparator_50_eq, comparator_51_eq);
  or or_3 (IType, or_2_out, comparator_52_eq);
  Comparator #(.width(7), .mode("unsigned")) comparator_52 (
    .a(OPCODE), .b(7'b1100111), .eq(comparator_52_eq));  // open: gt, lt
  Comparator #(.width(3), .mode("unsigned")) comparator_53 (
    .a(FUNCT3), .b(3'b000), .eq(comparator_53_eq));  // open: gt, lt
  Comparator #(.width(3), .mode("unsigned")) comparator_54 (
    .a(FUNCT3), .b(3'b000), .eq(comparator_54_eq));  // open: gt, lt
  Comparator #(.width(3), .mode("unsigned")) comparator_55 (
    .a(FUNCT3), .b(3'b001), .eq(comparator_55_eq));  // open: gt, lt
  Comparator #(.width(3), .mode("unsigned")) comparator_56 (
    .a(FUNCT3), .b(3'b001), .eq(comparator_56_eq));  // open: gt, lt
  Comparator #(.width(3), .mode("unsigned")) comparator_57 (
    .a(FUNCT3), .b(3'b100), .eq(comparator_57_eq));  // open: gt, lt
  Comparator #(.width(3), .mode("unsigned")) comparator_58 (
    .a(FUNCT3), .b(3'b100), .eq(comparator_58_eq));  // open: gt, lt
  Comparator #(.width(3), .mode("unsigned")) comparator_59 (
    .a(FUNCT3), .b(3'b110), .eq(comparator_59_eq));  // open: gt, lt
  Comparator #(.width(3), .mode("unsigned")) comparator_60 (
    .a(FUNCT3), .b(3'b110), .eq(comparator_60_eq));  // open: gt, lt
  Comparator #(.width(3), .mode("unsigned")) comparator_61 (
    .a(FUNCT3), .b(3'b100), .eq(comparator_61_eq));  // open: gt, lt
  Comparator #(.width(3), .mode("unsigned")) comparator_62 (
    .a(FUNCT3), .b(3'b110), .eq(comparator_62_eq));  // open: gt, lt
  and and_38 (and_38_out, BType, comparator_53_eq);
  and and_39 (and_39_out, BType, comparator_54_eq);
  not not_2 (not_2_out, BrEq);
  and and_40 (and_40_out, BType, comparator_55_eq);
  not not_3 (not_3_out, BrEq);
  and and_41 (and_41_out, BType, comparator_56_eq);
  and and_42 (and_42_out, BType, comparator_57_eq);
  and and_43 (and_43_out, BType, comparator_58_eq);
  not not_4 (not_4_out, BrLt);
  and and_44 (and_44_out, BType, comparator_59_eq);
  and and_45 (and_45_out, BType, comparator_60_eq);
  not not_5 (not_5_out, BrLt);
  and and_46 (and_46_out, BType, comparator_61_eq);
  and and_47 (and_47_out, BType, comparator_62_eq);
  Multiplexer #(.enable("false")) multiplexer_37 (.in1(1'b0), .out(PCSel), .sel(and_48_out));  // open: in0
  and and_48 (and_48_out, and_38_out, BrEq);
  Multiplexer #(.enable("false")) multiplexer_38 (.in1(1'b1), .out(PCSel), .sel(and_49_out));  // open: in0
  and and_49 (and_49_out, and_39_out, not_2_out);
  Multiplexer #(.enable("false")) multiplexer_39 (.in1(1'b0), .out(PCSel), .sel(and_50_out));  // open: in0
  and and_50 (and_50_out, and_40_out, not_3_out);
  Multiplexer #(.enable("false")) multiplexer_40 (.in1(1'b1), .out(PCSel), .sel(and_51_out));  // open: in0
  and and_51 (and_51_out, and_41_out, BrEq);
  Multiplexer #(.enable("false")) multiplexer_41 (.in1(1'b0), .out(PCSel), .sel(and_52_out));  // open: in0
  and and_52 (and_52_out, and_42_out, BrLt);
  Multiplexer #(.enable("false")) multiplexer_42 (.in1(1'b1), .out(PCSel), .sel(and_53_out));  // open: in0
  and and_53 (and_53_out, and_43_out, not_4_out);
  Multiplexer #(.enable("false")) multiplexer_43 (.in1(1'b0), .out(PCSel), .sel(and_54_out));  // open: in0
  and and_54 (and_54_out, and_44_out, BrLt);
  Multiplexer #(.enable("false")) multiplexer_44 (.in1(1'b1), .out(PCSel), .sel(and_55_out));  // open: in0
  and and_55 (and_55_out, and_45_out, not_5_out);
  Multiplexer #(.enable("false")) multiplexer_45 (.in1(1'b0), .out(BrUn), .sel(and_46_out));  // open: in0
  Multiplexer #(.enable("false")) multiplexer_46 (.in1(1'b1), .out(BrUn), .sel(and_47_out));  // open: in0
  Comparator #(.width(7), .mode("unsigned")) comparator_63 (.a(OPCODE), .b(7'b1100011), .eq(BType));  // open: gt, lt
  Multiplexer #(.enable("false")) multiplexer_47 (.in1(1'b1), .out(BSel), .sel(BType));  // open: in0
  Multiplexer #(.width(4), .enable("false")) multiplexer_48 (.in1(4'b0000), .out(ALUSel), .sel(BType));  // open: in0
  Multiplexer #(.enable("false")) multiplexer_49 (.in1(1'b0), .out(RegWEn), .sel(BType));  // open: in0
  Multiplexer #(.enable("false")) multiplexer_50 (.in1(1'b0), .out(ASel), .sel(BType));  // open: in0
  Multiplexer #(.enable("false")) multiplexer_51 (.in1(1'b0), .out(MemRW), .sel(BType));  // open: in0
  Comparator #(.width(3), .mode("unsigned")) comparator_64 (
    .a(FUNCT3), .b(3'b010), .eq(comparator_64_eq));  // open: gt, lt
  Comparator #(.width(7), .mode("unsigned")) comparator_65 (
    .a(OPCODE), .b(7'b0000011), .eq(comparator_65_eq));  // open: gt, lt
  Multiplexer #(.width(4), .enable("false")) multiplexer_52 (.in1(4'b0000), .out(ALUSel), .sel(lw));  // open: in0
  Multiplexer #(.enable("false")) multiplexer_53 (.in1(1'b1), .out(BSel), .sel(lw));  // open: in0
  Multiplexer #(.width(2), .enable("false")) multiplexer_54 (.in1(2'b01), .out(WBSel), .sel(lw));  // open: in0
  Multiplexer #(.enable("false")) multiplexer_55 (.in1(1'b1), .out(RegWEn), .sel(lw));  // open: in0
  Multiplexer #(.enable("false")) multiplexer_56 (.in1(1'b1), .out(ASel), .sel(lw));  // open: in0
  Multiplexer #(.enable("false")) multiplexer_57 (.in1(1'b0), .out(MemRW), .sel(lw));  // open: in0
  Multiplexer #(.enable("false")) multiplexer_58 (.in1(1'b1), .out(PCSel), .sel(lw));  // open: in0
  Comparator #(.width(3), .mode("unsigned")) comparator_66 (
    .a(FUNCT3), .b(3'b001), .eq(comparator_66_eq));  // open: gt, lt
  Comparator #(.width(7), .mode("unsigned")) comparator_67 (
    .a(OPCODE), .b(7'b0000011), .eq(comparator_67_eq));  // open: gt, lt
  Comparator #(.width(3), .mode("unsigned")) comparator_68 (
    .a(FUNCT3), .b(3'b000), .eq(comparator_68_eq));  // open: gt, lt
  Comparator #(.width(7), .mode("unsigned")) comparator_69 (
    .a(OPCODE), .b(7'b1100111), .eq(comparator_69_eq));  // open: gt, lt
  Multiplexer #(.enable("false")) multiplexer_59 (.in1(1'b1), .out(lw), .sel(and_56_out));  // open: in0
  and and_56 (and_56_out, comparator_64_eq, comparator_65_eq);
  and and_57 (and_57_out, comparator_66_eq, comparator_67_eq);
  and and_58 (and_58_out, comparator_68_eq, comparator_69_eq);
  Multiplexer #(.width(4), .enable("false")) multiplexer_60 (
    .in1(4'b0000), .out(ALUSel), .sel(and_57_out));  // open: in0
  Multiplexer #(.width(4), .enable("false")) multiplexer_61 (
    .in1(4'b0000), .out(ALUSel), .sel(and_58_out));  // open: in0
  Comparator #(.width(3), .mode("unsigned")) comparator_70 (
    .a(FUNCT3), .b(3'b000), .eq(comparator_70_eq));  // open: gt, lt
  Comparator #(.width(7), .mode("unsigned")) comparator_71 (
    .a(OPCODE), .b(7'b0000011), .eq(comparator_71_eq));  // open: gt, lt
  Multiplexer #(.width(4), .enable("false")) multiplexer_62 (.in1(4'b0000), .out(ALUSel), .sel(lb));  // open: in0
  Multiplexer #(.enable("false")) multiplexer_63 (.in1(1'b1), .out(BSel), .sel(lw));  // open: in0
  Multiplexer #(.width(2), .enable("false")) multiplexer_64 (.in1(2'b01), .out(WBSel), .sel(lw));  // open: in0
  Multiplexer #(.enable("false")) multiplexer_65 (.in1(1'b1), .out(RegWEn), .sel(lw));  // open: in0
  Multiplexer #(.enable("false")) multiplexer_66 (.in1(1'b1), .out(ASel), .sel(lw));  // open: in0
  Multiplexer #(.enable("false")) multiplexer_67 (.in1(1'b0), .out(MemRW), .sel(lw));  // open: in0
  Multiplexer #(.enable("false")) multiplexer_68 (.in1(1'b1), .out(PCSel), .sel(lw));  // open: in0
  Multiplexer #(.enable("false")) multiplexer_69 (.in1(1'b1), .out(lb), .sel(and_59_out));  // open: in0
  and and_59 (and_59_out, comparator_70_eq, comparator_71_eq);

  // Other names for the same wires on the sheet: OP0[3:0] = OPCODE[3:0]; OP1[2:0] = OPCODE[6:4]

  // Notes on the sheet:
  //   add
  //   mul
  //   sub
  //   sll
  //   mulh
  //   mulhu
  //   slt
  //   xor
  //   divu
  //   srl
  //   or
  //   remu
  //   and
  //   ALUSel for Rtype
  //   Other controls for Rtype
  //   ImmSel for any type
  //   addi
  //   slli
  //   slti
  //   xori
  //   srli
  //   srai
  //   ori
  //   andi
  //   ALUSel for Itype-exclude
  //   Other controls for Itype-exclude
  //   beq
  //   bne
  //   blt
  //   bltu
  //   blt
  //   bltu
  //   PCSel for Btype
  //   BrUn for Btype
  //   Other controls for Btype
  //   lh
  //   lw
  //   jalr
  //   lw
  //   lb
endmodule

module immgen (
  input  [31:0] INSTRUCTION,
  input  [2:0] IMMSEL,
  output [19:0] Immediate
);

  wire [19:0] bit_extender_1_out, bit_extender_2_out, bit_extender_3_out;

  assign bit_extender_1_out = {{8{INSTRUCTION[31]}}, INSTRUCTION[31:20]};  // Bit_Extender bit_extender_1
  assign bit_extender_2_out = {{8{INSTRUCTION[31]}}, {INSTRUCTION[31:25], INSTRUCTION[11:7]}};  // Bit_Extender bit_extender_2
  assign bit_extender_3_out = {{8{INSTRUCTION[31]}}, {INSTRUCTION[31], INSTRUCTION[7], INSTRUCTION[30:25], INSTRUCTION[11:8]}};  // Bit_Extender bit_extender_3
  Multiplexer #(.select(3), .width(20), .enable("false")) multiplexer_1 (
    .in1(bit_extender_1_out), .in2(bit_extender_2_out), .in3(bit_extender_3_out), .in4(INSTRUCTION[31:12]),
    .in5({INSTRUCTION[31], INSTRUCTION[19:12], INSTRUCTION[20], INSTRUCTION[30:21]}), .out(Immediate),
    .sel(IMMSEL));  // open: in0, in6, in7

  // Other names for the same wires on the sheet: B[11:0] = {INSTRUCTION[31], INSTRUCTION[7], INSTRUCTION[30:25], INSTRUCTION[11:8]};
  //   rd[4:0] = INSTRUCTION[11:7]; S[11:0] = {INSTRUCTION[31:25], INSTRUCTION[11:7]}; opcode[6:0] = INSTRUCTION[6:0];
  //   I[11:0] = INSTRUCTION[31:20];
  //   J[19:0] = {INSTRUCTION[31], INSTRUCTION[19:12], INSTRUCTION[20], INSTRUCTION[30:21]};
  //   rs2[4:0] = INSTRUCTION[24:20]; U[19:0] = INSTRUCTION[31:12]; funct7[6:0] = INSTRUCTION[31:25];
  //   funct3[2:0] = INSTRUCTION[14:12]; rs1[4:0] = INSTRUCTION[19:15]
endmodule

// BrLt
module branch (
  input  [31:0] rs1,
  input  [31:0] rs2,
  input  in_3,
  output BrEq,
  output BrLt
);

  wire comparator_1_lt, comparator_2_lt;

  Comparator #(.width(32)) comparator_1 (.a(rs1), .b(rs2), .eq(BrEq), .lt(comparator_1_lt));  // open: gt
  Comparator #(.width(32), .mode("unsigned")) comparator_2 (.a(rs1), .b(rs2), .lt(comparator_2_lt));  // open: gt, eq
  Multiplexer #(.enable("false")) multiplexer_1 (.in0(comparator_1_lt), .in1(comparator_2_lt), .out(BrLt), .sel(in_3));

  // Other names for the same wires on the sheet: BrUn = in_3
endmodule
