// Logisim project alu.circ as structural Verilog: 1 circuit, main circuit alu
module alu (
  input  [31:0] A,
  input  [31:0] B,
  input  [3:0] ALUSel,
  output [31:0] Result
);

  wire comparator_1_lt;
  wire [31:0] add0, and0, div0, divider_2_out, mul0, mulh0, mulhu0, multiplier_4_cout, multiplier_5_cout,
       negator_1_out, negator_2_out, negator_3_out, negator_4_out, NN, NP, or0, PN, PP, remu0, sll0, slt0,
       sra0, srl0, sub0, xor0;

  assign and0 = A & B;  // AND_Gate and_1, 32 bits wide
  Shifter #(.width(32)) shifter_1 (.in(A), .\dist (B[4:0]), .out(sll0));
  Multiplier #(.width(32)) multiplier_1 (.a(A), .b(B), .out(mul0), .cout(PP));  // open: cin
  Multiplexer #(.select(2), .width(32), .enable("false")) multiplexer_1 (
    .in0(PP), .in1(NP), .in2(PN), .in3(NN), .out(mulh0), .sel({B[31], A[31]}));
  assign or0 = A | B;  // OR_Gate or_1, 32 bits wide
  Comparator #(.width(32)) comparator_1 (.a(A), .b(B), .lt(comparator_1_lt));  // open: gt, eq
  Multiplier #(.width(32)) multiplier_2 (.a(A), .b(B), .cout(mulhu0));  // open: out, cin
  Negator #(.width(32)) negator_1 (.in(A), .out(negator_1_out));
  Negator #(.width(32)) negator_2 (.in(B), .out(negator_2_out));
  assign slt0 = {{31{1'b0}}, comparator_1_lt};  // Bit_Extender bit_extender_1
  Multiplier #(.width(32)) multiplier_3 (.a(negator_1_out), .b(negator_2_out), .cout(NN));  // open: out, cin
  Adder #(.width(32)) adder_1 (.a(A), .b(B), .out(add0));  // open: cin, cout
  assign xor0 = A ^ B;  // XOR_Gate xor_1, 32 bits wide
  Divider #(.width(32)) divider_1 (.a(A), .b(B), .out(div0));  // open: upper, rem
  Subtractor #(.width(32)) subtractor_1 (.a(A), .b(B), .out(sub0));  // open: bin, bout
  Negator #(.width(32)) negator_3 (.in(A), .out(negator_3_out));
  Multiplier #(.width(32)) multiplier_4 (.a(negator_3_out), .b(B), .cout(multiplier_4_cout));  // open: out, cin
  Shifter #(.width(32), .shift("lr")) shifter_2 (.in(A), .\dist (B[4:0]), .out(srl0));
  assign NP = ~multiplier_4_cout;  // NOT_Gate not_1, 32 bits wide
  Multiplexer #(.select(4), .width(32), .enable("false")) multiplexer_2 (
    .in0(add0), .in1(and0), .in2(or0), .in3(xor0), .in4(srl0), .in5(sra0), .in6(sll0), .in7(slt0),
    .in8(div0), .in9(remu0), .in10(mul0), .in11(mulhu0), .in12(sub0), .in13(B), .in14(mulh0), .out(Result),
    .sel(ALUSel));  // open: in15
  Divider #(.width(32)) divider_2 (.a(A), .b(B), .out(divider_2_out), .rem(remu0));  // open: upper
  Negator #(.width(32)) negator_4 (.in(B), .out(negator_4_out));
  Multiplier #(.width(32)) multiplier_5 (.a(A), .b(negator_4_out), .cout(multiplier_5_cout));  // open: out, cin
  assign PN = ~multiplier_5_cout;  // NOT_Gate not_2, 32 bits wide
  Shifter #(.width(32), .shift("ar")) shifter_3 (.in(A), .\dist (B[4:0]), .out(sra0));

  // Other names for the same wires on the sheet: bsel[31:0] = B

  // Notes on the sheet:
  //   INPUTS to your circuit
  //   DON'T CHANGE THE LOCATIONS OF THE INPUTS AND OUTPUTS!
  //   OUTPUT from your circuit
endmodule
