// Logisim project cpu.circ as structural Verilog: 1 circuit, main circuit main
module main (
  input  [31:0] INSTRUCTION,
  input  CLOCK,
  output [31:0] PROGRAM_COUNTER,
  output [31:0] ra,
  output [31:0] sp,
  output [31:0] t0,
  output [31:0] t1,
  output [31:0] t2,
  output [31:0] s0,
  output [31:0] s1,
  output [31:0] a0
);

  wire [2:0] funct3;
  wire [11:0] imm;
  wire [19:0] INSTRUCTION1;
  wire [31:0] adder_1_out, Arithmetic_Logic_Unit_result, immout, multiplexer_1_out, rs1out;

  Adder #(.width(32)) adder_1 (.a(PROGRAM_COUNTER), .b(32'h4), .out(adder_1_out));  // open: cin, cout
  Register #(.width(32)) PC (.D(adder_1_out), .clk(CLOCK), .Q(PROGRAM_COUNTER));  // open: en, clr
  assign immout = {{20{imm[11]}}, imm};  // Bit_Extender bit_extender_1
  Register #(.width(32)) register_1 (
    .D(INSTRUCTION), .clk(CLOCK), .Q({imm, INSTRUCTION1[19:15], funct3, INSTRUCTION1[11:0]}));  // open: en, clr
  regfile_main RegFile (
    .rd(INSTRUCTION1[11:7]), .Read_Data_1(rs1out), .ra(ra), .sp(sp), .t0(t0), .t1(t1), .t2(t2), .s0(s0),
    .s1(s1), .a0(a0), .rs1(INSTRUCTION1[19:15]), .Write_Data(multiplexer_1_out), .RegWEn(1'b1), .clk(CLOCK));  // open: rs2, Read_Data_2
  alu Arithmetic_Logic_Unit (.Result(Arithmetic_Logic_Unit_result), .ALUSel(4'b0000), .A(rs1out), .B(immout));
  Multiplexer #(.select(2), .width(32), .enable("false")) multiplexer_1 (
    .in0(Arithmetic_Logic_Unit_result), .out(multiplexer_1_out), .sel(2'b00));  // open: in1, in2, in3
  // mem_main DMEM: pin names not known; wires that end beside it: CLOCK

  // Other names for the same wires on the sheet: clk = CLOCK; opcode[6:0] = INSTRUCTION1[6:0];
  //   rd[4:0] = INSTRUCTION1[11:7]; INSTRUCTION1 (some bits) = {imm, funct3}; rs1[4:0] = INSTRUCTION1[19:15]

  // Notes on the sheet:
  //   Output
  //   IMEM (do **NOT** move this)
  //   Inputs
  //   Inputs/Outputs for testing. Do **NOT** move these.
endmodule
