// Logisim project regfile.circ as structural Verilog: 1 circuit, main circuit main
module main (
  input  [4:0] rs1,
  input  [4:0] rs2,
  input  [4:0] rd,
  input  [31:0] Write_Data,
  input  RegWEn,
  input  clk,
  output [31:0] ra,
  output [31:0] sp,
  output [31:0] t0,
  output [31:0] t1,
  output [31:0] t2,
  output [31:0] s0,
  output [31:0] s1,
  output [31:0] a0,
  output [31:0] Read_Data_1,
  output [31:0] Read_Data_2
);

  wire a00, demultiplexer_1_out0, ra0, s00, s10, sp0, t00, t10, t20;
  wire [31:0] multiplexer_1_out, multiplexer_2_out, multiplexer_3_out, multiplexer_4_out, multiplexer_7_out,
       multiplexer_8_out, multiplexer_9_out, multiplexer_10_out, zero;

  Register #(.width(32)) register_1 (.D(zero), .clk(clk), .Q(zero));  // open: en, clr
  Register #(.width(32)) register_2 (.D(multiplexer_1_out), .en(RegWEn), .clk(clk), .Q(ra));  // open: clr
  Multiplexer #(.width(32), .enable("false")) multiplexer_1 (
    .in0(ra), .in1(Write_Data), .out(multiplexer_1_out), .sel(ra0));
  Register #(.width(32)) register_3 (.D(multiplexer_2_out), .en(RegWEn), .clk(clk), .Q(sp));  // open: clr
  Multiplexer #(.width(32), .enable("false")) multiplexer_2 (
    .in0(sp), .in1(Write_Data), .out(multiplexer_2_out), .sel(sp0));
  Register #(.width(32)) register_4 (.D(multiplexer_3_out), .en(RegWEn), .clk(clk), .Q(t0));  // open: clr
  Multiplexer #(.width(32), .enable("false")) multiplexer_3 (
    .in0(t0), .in1(Write_Data), .out(multiplexer_3_out), .sel(t00));
  Register #(.width(32)) register_5 (.D(multiplexer_4_out), .en(RegWEn), .clk(clk), .Q(t1));  // open: clr
  Multiplexer #(.width(32), .enable("false")) multiplexer_4 (
    .in0(t1), .in1(Write_Data), .out(multiplexer_4_out), .sel(t10));
  Multiplexer #(.select(5), .width(32), .enable("false")) multiplexer_5 (
    .in0(zero), .in1(ra), .in2(sp), .in5(t0), .in6(t1), .in7(t2), .in8(s0), .in9(s1), .in10(a0),
    .out(Read_Data_1), .sel(rs1));  // open: in3, in4, in11, in12, in13, in14, in15, in16, in17, in18, in19, in20, in21, in22, in23, in24, in25, in26, in27, in28, in29, in30, in31
  Multiplexer #(.select(5), .width(32), .enable("false")) multiplexer_6 (
    .in0(zero), .in1(ra), .in2(sp), .in5(t0), .in6(t1), .in7(t2), .in8(s0), .in9(s1), .in10(a0),
    .out(Read_Data_2), .sel(rs2));  // open: in3, in4, in11, in12, in13, in14, in15, in16, in17, in18, in19, in20, in21, in22, in23, in24, in25, in26, in27, in28, in29, in30, in31
  Demultiplexer #(.select(5), .enable("false")) demultiplexer_1 (
    .out0(demultiplexer_1_out0), .out1(ra0), .out2(sp0), .out5(t00), .out6(t10), .out7(t20), .out8(s00),
    .out9(s10), .out10(a00), .in(RegWEn), .sel(rd));  // open: out3, out4, out11, out12, out13, out14, out15, out16, out17, out18, out19, out20, out21, out22, out23, out24, out25, out26, out27, out28, out29, out30, out31
  Register #(.width(32)) register_6 (.D(multiplexer_7_out), .en(RegWEn), .clk(clk), .Q(t2));  // open: clr
  Multiplexer #(.width(32), .enable("false")) multiplexer_7 (
    .in0(t2), .in1(Write_Data), .out(multiplexer_7_out), .sel(t20));
  Register #(.width(32)) register_7 (.D(multiplexer_8_out), .en(RegWEn), .clk(clk), .Q(s0));  // open: clr
  Multiplexer #(.width(32), .enable("false")) multiplexer_8 (
    .in0(s0), .in1(Write_Data), .out(multiplexer_8_out), .sel(s00));
  Register #(.width(32)) register_8 (.D(multiplexer_9_out), .en(RegWEn), .clk(clk), .Q(s1));  // open: clr
  Multiplexer #(.width(32), .enable("false")) multiplexer_9 (
    .in0(s1), .in1(Write_Data), .out(multiplexer_9_out), .sel(s10));
  Register #(.width(32)) register_9 (.D(multiplexer_10_out), .en(RegWEn), .clk(clk), .Q(a0));  // open: clr
  Multiplexer #(.width(32), .enable("false")) multiplexer_10 (
    .in0(a0), .in1(Write_Data), .out(multiplexer_10_out), .sel(a00));

  // Other names for the same wires on the sheet: read_data1[31:0] = Read_Data_1; read_data2[31:0] = Read_Data_2;
  //   read_reg1[4:0] = rs1; read_reg2[4:0] = rs2; write_en = RegWEn; write_reg[4:0] = rd

  // Notes on the sheet:
  //   INPUTS to your circuit
  //   DON'T CHANGE THE LOCATIONS OF THE INPUTS AND OUTPUTS!
  //   These are DEBUG/TEST outputs from your circuit.
  //   OUTPUTS from your circuit
endmodule
